# Fritzing sketch diagram (saved by Fritzing 0.9.10b)

parts:
  Part2 = Arduino Pro Mini v13
  U1 = LIPO-1000mAh [package=lipo-1000]
  J1 = female pin header, 2 pins [form="♀ (female)"]
  J2 = female pin header, 2 pins [form="♀ (female)"]
  J3 = Power Jack [package=power_jack_combo]
  Mod2 = zmpt101b
  A1 = j5019
  M2 = ESP-01 Adapter [part_number=ESP8266]

nets:
  N1: Part2.RAW, A1.Pin_1
  N2: Part2.GND, U1.-, J3.GNDBREAK, A1.Pin_2, A1.Pin_4, A1.Pin_5
  N3: Part2.A0, Mod2.OUT
  N4: Part2.D11_PWM/MOSI, M2.RX
  N5: Part2.D10_PWM/SS, M2.TX
  N6: U1.+, A1.Pin_6
  N7: J1.pin1, M2.VCC
  N8: J1.pin2, M2.GND
  N9: J2.pin1, Mod2.VCC
  N10: J2.pin2, Mod2.GND
  N11: J3.PWR, A1.Pin_3

custom parts:
  zmpt101b: Single phase ac active output voltate transformer module.
  j5019: This module is a small single cell lithium battery charging module which also includes a 1A step-up (boost) converter for powering a large range of applications.
  ESP-01 Adapter: Generic ESP-10 Adapter module with ESP8266 wireless module installed.
